# Fritzing sketch vca-lm13700 (saved by Fritzing 0.9.6b)
stripboards: 1

parts:
  R7 = Resistor [tolerance=±5% power=0.25 resistance=330k package=THT]
  R9 = Resistor [tolerance=±5% power=0.25 resistance=330k package=THT]
  R6 = Resistor [tolerance=±5% power=0.25 resistance=330k package=THT]
  R10 = Resistor [tolerance=±5% power=0.25 resistance=33k package=THT]
  R11 = Resistor [tolerance=±5% power=0.25 resistance=1k package=THT]
  D1 = Rectifier Diode [part_number=1N4148 package="300 mil [THT]"]
  C1 = Ceramic Capacitor [capacitance=1nF voltage=35V package="100 mil [THT, multilayer]"]
  IC1 = TL074 Quad Opamp (Movable) [package="DIP (Dual Inline)"]  # not connected
  IC1_PWR = TL074 Quad Opamp (Movable) [package="DIP (Dual Inline)"]
  IC1_A = TL074 Quad Opamp (Movable) [package="DIP (Dual Inline)"]
  IC1_B = TL074 Quad Opamp (Movable) [package="DIP (Dual Inline)"]
  IC1_C = TL074 Quad Opamp (Movable) [package="DIP (Dual Inline)"]
  IC1_D = TL074 Quad Opamp (Movable) [package="DIP (Dual Inline)"]
  VR2 = Trimmer Potentiometer [maximum_resistance=100kΩ package=THT]
  R8 = Resistor [tolerance=±5% power=0.25 resistance=6800 package=THT]
  IC2 = OTA [package="DIP (Dual Inline) [THT]"]  # not connected
  IC2_1 = OTA [package="DIP (Dual Inline) [THT]"]
  IC2_2 = OTA [package="DIP (Dual Inline) [THT]"]
  IC2_3 = OTA [package="DIP (Dual Inline) [THT]"]
  IC2_4 = OTA [package="DIP (Dual Inline) [THT]"]
  Part1 = OTA [package="DIP (Dual Inline) [THT]"]
  C2 = Ceramic Capacitor [capacitance=470nF voltage=35V package="100 mil [THT, multilayer]"]
  R1 = Resistor [tolerance=±5% power=0.25 resistance=100k package=THT]
  R2 = Resistor [tolerance=±5% power=0.25 resistance=620 package=THT]
  R3 = Resistor [tolerance=±5% power=0.25 resistance=620 package=THT]
  R4 = Resistor [tolerance=±5% power=0.25 resistance=220 package=THT]
  R5 = Resistor [tolerance=±5% power=0.25 resistance=1k package=THT]
  C6 = Electrolytic Capacitor [capacitance=1µF voltage=35V package="100 mil [THT, electrolytic]"]
  C5 = Electrolytic Capacitor [capacitance=1µF voltage=35V package="100 mil [THT, electrolytic]"]
  J1 = shrouded pin header, 10 pins [form="♂ (shrouded male)"]
  R12 = Resistor [tolerance=±5% resistance=120k power=0.25 package=THT]
  Q1 = PNP-Transistor [package="TO92 [THT]"]
  VR1 = Trimmer Potentiometer [maximum_resistance=100kΩ package=THT]
  R19 = Resistor [tolerance=±5% power=0.25 resistance=1k package=THT]
  R20 = Resistor [tolerance=±5% power=0.25 resistance=220 package=THT]
  R22 = Resistor [tolerance=±5% power=0.25 resistance=620 package=THT]
  R23 = Resistor [tolerance=±5% power=0.25 resistance=100k package=THT]
  R21 = Resistor [tolerance=±5% power=0.25 resistance=620 package=THT]
  C7 = Ceramic Capacitor [capacitance=470nF voltage=35V package="100 mil [THT, multilayer]"]
  Q2 = PNP-Transistor [package="TO92 [THT]"]
  R14 = Resistor [tolerance=±5% power=0.25 resistance=680k package=THT]
  D2 = Rectifier Diode [part_number=1N4148 package="300 mil [THT]"]
  VR3 = Trimmer Potentiometer [maximum_resistance=100kΩ package=THT]
  R17 = Resistor [tolerance=±5% power=0.25 resistance=330k package=THT]
  R13 = Resistor [tolerance=±5% power=0.25 resistance=120 package=THT]
  VR4 = Trimmer Potentiometer [maximum_resistance=100kΩ package=THT]
  R18 = Resistor [tolerance=±5% power=0.25 resistance=33k package=THT]
  R16 = Resistor [tolerance=±5% power=0.25 resistance=330k package=THT]
  R15 = Resistor [tolerance=±5% power=0.25 resistance=330k package=THT]
  C8 = Ceramic Capacitor [capacitance=1nF voltage=35V package="100 mil [THT, multilayer]"]
  R24 = Resistor [tolerance=±5% power=0.25 resistance=1k package=THT]

nets (from the schematic view):
  N1: R7.Pin_0, VR1.wiper
  N2: R7.Pin_1, R9.Pin_1, R6.Pin_1, R10.Pin_0, D1.cathode, C1.1, IC1_A.1IN-
  ADSR: R9.Pin_0
  N3: R6.Pin_0, VR2.wiper
  N4: R10.Pin_1, R11.Pin_0, Q1.E
  GND: R11.Pin_1, IC1_A.1IN+, IC1_B.2IN+, IC1_C.3IN-, IC1_D.4IN-, VR2.leg1, IC2_2.pin7, IC2_4.pin10, R2.Pin_0, R3.Pin_0, C6.+, C5.-, J1.pin2, J1.pin3, J1.pin4, J1.pin7, J1.pin8, J1.pin9, R22.Pin_0, R21.Pin_0, VR3.leg1, R24.Pin_1
  N5: D1.anode, C1.0, IC1_A.1OUT, Q1.B
  12V: IC1_PWR.VCC+, IC2_2.pin11, C5.+, J1.pin5, J1.pin6, R12.Pin_0, R13.Pin_0
  -12V: IC1_PWR.VCC-, Part1.pin6, C6.-, J1.pin1, J1.pin10, VR1.leg1, VR4.leg1
  N6: IC1_B.2IN-, IC2_1.pin5, R4.Pin_0
  N7: IC1_B.2OUT, R4.Pin_1, R5.Pin_0
  N8: IC1_C.3OUT, Q2.B, D2.anode, C8.0
  N9: IC1_C.3IN+, D2.cathode, R17.Pin_1, R18.Pin_0, R16.Pin_1, R15.Pin_1, C8.1
  N10: IC1_D.4IN+, IC2_3.pin12, R20.Pin_0
  N11: IC1_D.4OUT, R19.Pin_0, R20.Pin_1
  Gain CV: VR2.leg2
  N12: R8.Pin_0, IC2_1.pin1
  N13: R8.Pin_1, Q1.C
  N14: IC2_1.pin3, R3.Pin_1
  N15: IC2_1.pin4, R1.Pin_1, R2.Pin_1
  N16: IC2_3.pin13, R22.Pin_1, R23.Pin_1
  N17: IC2_3.pin14, R21.Pin_1
  N18: IC2_3.pin16, R14.Pin_0
  N19: C2.0, R1.Pin_0
  Audio IN: C2.1
  Out: R5.Pin_1
  N20: R12.Pin_1, VR1.leg2
  Second Out: R19.Pin_1
  N21: R23.Pin_0, C7.0
  Second Audio In: C7.1
  N22: Q2.E, R18.Pin_1, R24.Pin_0
  N23: Q2.C, R14.Pin_1
  N24: VR3.wiper, R15.Pin_0
  Second CV Gain: VR3.leg2
  N25: R17.Pin_0, VR4.wiper
  N26: R13.Pin_1, VR4.leg2
  Second ADSR: R16.Pin_0

custom parts:
  TL074 Quad Opamp (Movable): Quadruple Operational Amplifier (Opamp)
  TL074 Quad Opamp (Movable): Quadruple Operational Amplifier (Opamp)
  TL074 Quad Opamp (Movable): Quadruple Operational Amplifier (Opamp)
  TL074 Quad Opamp (Movable): Quadruple Operational Amplifier (Opamp)
  TL074 Quad Opamp (Movable): Quadruple Operational Amplifier (Opamp)
  TL074 Quad Opamp (Movable): Quadruple Operational Amplifier (Opamp)
  OTA: Operational Transconductance Amplifier
  OTA: Operational Transconductance Amplifier
  OTA: Operational Transconductance Amplifier
  OTA: Operational Transconductance Amplifier
  OTA: Operational Transconductance Amplifier
  OTA: Operational Transconductance Amplifier
